// Logisim project Practico 3.circ as structural Verilog: 11 circuits, main circuit prueba
module prueba (
  input  a,
  input  b,
  input  c,
  output x,
  output y,
  output z
);

  wire not_1_out, not_2_out, not_3_out, not_4_out, not_5_out;

  not not_1 (not_1_out, b);
  not not_2 (not_2_out, a);
  not not_3 (not_3_out, b);
  not not_4 (not_4_out, b);
  not not_5 (not_5_out, c);
  and and_1 (x, a, not_1_out, c);
  and and_2 (y, not_2_out, not_3_out, c);
  and and_3 (z, a, not_4_out, not_5_out);
endmodule

module DU (
  input  IR13,
  input  IR12,
  input  IR11,
  input  IR10,
  input  IR9,
  input  IR8,
  output OUTwe,
  output Incond,
  output Cond,
  output REGwe,
  output ALUop2,
  output ALUop1,
  output ALUop0,
  output REGAwe,
  output INen,
  output REGen,
  output INMen
);

  wire and_3_out, and_4_out, and_5_out, and_6_out, and_7_out, and_8_out, and_9_out, and_10_out, and_11_out,
       and_12_out, and_13_out, and_14_out, and_15_out, and_16_out, and_19_out, and_20_out, and_21_out,
       and_22_out, and_23_out, and_24_out, and_25_out, not_1_out, not_2_out, not_3_out, not_4_out, not_5_out,
       not_6_out, not_7_out, not_8_out, not_9_out, not_10_out, not_11_out, not_12_out, not_13_out,
       not_14_out, not_15_out, not_16_out, not_17_out, not_18_out, not_19_out, not_20_out, not_21_out,
       not_22_out, not_23_out, not_24_out, not_25_out, not_26_out, not_27_out, not_28_out, not_29_out,
       not_30_out, not_31_out, not_32_out, not_33_out, not_34_out, not_35_out, not_36_out, not_37_out,
       not_38_out, not_39_out, not_40_out, not_41_out, not_42_out, not_43_out, not_44_out, not_45_out,
       not_46_out, not_47_out, not_48_out, not_49_out, not_50_out, not_51_out, not_52_out, not_53_out,
       not_54_out, not_55_out, not_56_out, not_57_out, not_58_out, not_59_out, not_60_out, not_61_out,
       not_62_out, not_63_out, not_64_out, not_65_out, not_66_out, not_67_out, not_68_out, not_69_out,
       not_70_out, not_71_out, not_72_out, not_73_out, not_74_out, not_75_out, not_76_out, not_77_out,
       not_78_out, not_79_out, not_80_out, not_81_out, not_82_out, not_83_out, not_84_out, not_85_out,
       not_86_out, not_87_out, not_88_out, not_89_out, not_90_out, not_91_out, not_92_out;

  not not_1 (not_1_out, IR13);
  not not_2 (not_2_out, IR12);
  not not_3 (not_3_out, IR11);
  not not_4 (not_4_out, IR10);
  not not_5 (not_5_out, IR8);
  not not_6 (not_6_out, IR11);
  not not_7 (not_7_out, IR10);
  not not_8 (not_8_out, IR9);
  not not_9 (not_9_out, IR8);
  not not_10 (not_10_out, IR11);
  not not_11 (not_11_out, IR10);
  not not_12 (not_12_out, IR9);
  not not_13 (not_13_out, IR11);
  not not_14 (not_14_out, IR10);
  not not_15 (not_15_out, IR8);
  not not_16 (not_16_out, IR13);
  not not_17 (not_17_out, IR11);
  not not_18 (not_18_out, IR10);
  not not_19 (not_19_out, IR13);
  not not_20 (not_20_out, IR11);
  not not_21 (not_21_out, IR10);
  not not_22 (not_22_out, IR13);
  not not_23 (not_23_out, IR11);
  not not_24 (not_24_out, IR9);
  not not_25 (not_25_out, IR8);
  not not_26 (not_26_out, IR12);
  not not_27 (not_27_out, IR11);
  not not_28 (not_28_out, IR10);
  not not_29 (not_29_out, IR9);
  not not_30 (not_30_out, IR13);
  not not_31 (not_31_out, IR11);
  not not_32 (not_32_out, IR10);
  not not_33 (not_33_out, IR13);
  not not_34 (not_34_out, IR11);
  not not_35 (not_35_out, IR9);
  not not_36 (not_36_out, IR8);
  not not_37 (not_37_out, IR12);
  not not_38 (not_38_out, IR11);
  not not_39 (not_39_out, IR10);
  not not_40 (not_40_out, IR9);
  not not_41 (not_41_out, IR13);
  not not_42 (not_42_out, IR11);
  not not_43 (not_43_out, IR10);
  not not_44 (not_44_out, IR9);
  not not_45 (not_45_out, IR13);
  not not_46 (not_46_out, IR11);
  not not_47 (not_47_out, IR9);
  not not_48 (not_48_out, IR8);
  not not_49 (not_49_out, IR12);
  not not_50 (not_50_out, IR11);
  not not_51 (not_51_out, IR10);
  not not_52 (not_52_out, IR9);
  not not_53 (not_53_out, IR13);
  not not_54 (not_54_out, IR11);
  not not_55 (not_55_out, IR10);
  not not_56 (not_56_out, IR12);
  not not_57 (not_57_out, IR11);
  not not_58 (not_58_out, IR10);
  not not_59 (not_59_out, IR9);
  not not_60 (not_60_out, IR13);
  not not_61 (not_61_out, IR12);
  not not_62 (not_62_out, IR11);
  not not_63 (not_63_out, IR9);
  not not_64 (not_64_out, IR13);
  not not_65 (not_65_out, IR12);
  not not_66 (not_66_out, IR11);
  not not_67 (not_67_out, IR10);
  not not_68 (not_68_out, IR9);
  not not_69 (not_69_out, IR13);
  not not_70 (not_70_out, IR11);
  not not_71 (not_71_out, IR10);
  not not_72 (not_72_out, IR13);
  not not_73 (not_73_out, IR11);
  not not_74 (not_74_out, IR9);
  not not_75 (not_75_out, IR8);
  not not_76 (not_76_out, IR13);
  not not_77 (not_77_out, IR11);
  not not_78 (not_78_out, IR10);
  not not_79 (not_79_out, IR11);
  not not_80 (not_80_out, IR10);
  not not_81 (not_81_out, IR8);
  not not_82 (not_82_out, IR12);
  not not_83 (not_83_out, IR11);
  not not_84 (not_84_out, IR10);
  not not_85 (not_85_out, IR9);
  not not_86 (not_86_out, IR13);
  not not_87 (not_87_out, IR12);
  not not_88 (not_88_out, IR11);
  not not_89 (not_89_out, IR9);
  not not_90 (not_90_out, IR11);
  not not_91 (not_91_out, IR10);
  not not_92 (not_92_out, IR9);
  and and_1 (OUTwe, not_1_out, not_2_out, not_3_out, not_4_out, IR9, not_5_out);
  and and_2 (Incond, IR13, IR12, not_6_out, not_7_out, not_8_out, not_9_out);
  and and_3 (and_3_out, IR13, IR12, not_10_out, not_11_out, not_12_out, IR8);
  and and_4 (and_4_out, IR13, IR12, not_13_out, not_14_out, IR9, not_15_out);
  and and_5 (and_5_out, not_16_out, not_17_out, not_18_out, IR8);
  and and_6 (and_6_out, not_19_out, IR12, not_20_out, not_21_out);
  and and_7 (and_7_out, not_22_out, IR12, not_23_out, not_24_out, not_25_out);
  and and_8 (and_8_out, IR13, not_26_out, not_27_out, not_28_out, not_29_out);
  and and_9 (and_9_out, not_30_out, IR12, not_31_out, not_32_out, IR9);
  and and_10 (and_10_out, not_33_out, IR12, not_34_out, IR10, not_35_out, not_36_out);
  and and_11 (and_11_out, IR13, not_37_out, not_38_out, not_39_out, not_40_out, IR8);
  and and_12 (and_12_out, not_41_out, IR12, not_42_out, not_43_out, not_44_out);
  and and_13 (and_13_out, not_45_out, IR12, not_46_out, not_47_out, not_48_out);
  and and_14 (and_14_out, IR13, not_49_out, not_50_out, not_51_out, not_52_out, IR8);
  and and_15 (and_15_out, not_53_out, IR12, not_54_out, not_55_out, IR8);
  and and_16 (and_16_out, IR13, not_56_out, not_57_out, not_58_out, not_59_out);
  and and_17 (REGAwe, not_60_out, not_61_out, not_62_out, IR10, not_63_out);
  and and_18 (INen, not_64_out, not_65_out, not_66_out, not_67_out, not_68_out, IR8);
  and and_19 (and_19_out, not_69_out, not_70_out, not_71_out, IR9);
  and and_20 (and_20_out, not_72_out, not_73_out, IR10, not_74_out, not_75_out);
  and and_21 (and_21_out, not_76_out, IR12, not_77_out, not_78_out);
  and and_22 (and_22_out, IR12, not_79_out, not_80_out, IR9, not_81_out);
  and and_23 (and_23_out, IR13, not_82_out, not_83_out, not_84_out, not_85_out);
  and and_24 (and_24_out, not_86_out, not_87_out, not_88_out, IR10, not_89_out, IR8);
  and and_25 (and_25_out, IR13, IR12, not_90_out, not_91_out, not_92_out);
  or or_1 (Cond, and_3_out, and_4_out);
  or or_2 (REGwe, and_5_out, and_6_out, and_7_out, and_8_out);
  or or_3 (ALUop2, and_9_out, and_10_out, and_11_out);
  or or_4 (ALUop1, and_12_out, and_13_out, and_14_out);
  or or_5 (ALUop0, and_15_out, and_16_out);
  or or_6 (REGen, and_19_out, and_20_out, and_21_out, and_22_out, and_23_out);
  or or_7 (INMen, and_24_out, and_25_out);
endmodule

module Procesador (
  input  RESET,
  input  [7:0] INPUT,
  output [7:0] out_3
);

  wire ALU_op0, ALU_op1, ALU_op2, and_1_out, and_2_out, clk, Cond, IN_en, Incond, INM_en, not_1_out,
       or_1_out, or_2_out, OUT_we, REG_en, REG_we, REGA_we, Zero;
  wire [3:0] rd, rs;
  wire [7:0] alu_1_s, B, banco_de_registros_1_out, controlled_buffer_1_out;
  wire [15:0] rom_1_s;
  wire [15:8] register_1_q;

  and and_1 (and_1_out, Cond, Zero);
  or or_1 (or_1_out, Incond, and_1_out);
  or or_2 (or_2_out, RESET, or_1_out);
  assign controlled_buffer_1_out = IN_en ? INPUT : 8'bz;  // Controlled_Buffer controlled_buffer_1
  ROM rom_1 (.clk(clk), .Jump(or_2_out), .J_Address(controlled_buffer_1_out), .S(rom_1_s));
  assign controlled_buffer_1_out = RESET ? {8{1'b0}} : 8'bz;  // Controlled_Buffer controlled_buffer_2
  Register #(.width(16)) register_1 (
    .D(rom_1_s), .Q({register_1_q, rd, rs}), .clk(not_1_out), .clr(RESET));  // open: en
  not not_1 (not_1_out, clk);
  // Probe on alu_1_s
  Register REG_out (.D(alu_1_s), .en(OUT_we), .Q(out_3), .clk(clk), .clr(RESET));
  DU du_1 (
    .IR13(register_1_q[13]), .IR12(register_1_q[12]), .IR11(register_1_q[11]), .IR10(register_1_q[10]),
    .IR9(register_1_q[9]), .IR8(register_1_q[8]), .OUTwe(OUT_we), .Incond(Incond), .Cond(Cond),
    .REGwe(REG_we), .ALUop2(ALU_op2), .ALUop1(ALU_op1), .ALUop0(ALU_op0), .REGAwe(REGA_we), .INen(IN_en),
    .REGen(REG_en), .INMen(INM_en));
  assign controlled_buffer_1_out = INM_en ? {rd, rs} : 8'bz;  // Controlled_Buffer controlled_buffer_3
  Banco_de_Registros banco_de_registros_1 (
    .IN(alu_1_s), .We(REG_we), .Clk(clk), .Rst(RESET), .Rd(rd), .Rs(rs), .Out(banco_de_registros_1_out));
  // Probe on controlled_buffer_1_out
  assign controlled_buffer_1_out = REG_en ? banco_de_registros_1_out : 8'bz;  // Controlled_Buffer controlled_buffer_4
  // Probe on rs
  // Probe on rd
  ALU alu_1 (
    .A(controlled_buffer_1_out), .B(B), .Ctrl0(ALU_op0), .Ctrl1(ALU_op1), .Ctrl2(ALU_op2), .S(alu_1_s));  // open: Cout
  Register REG_A (.D(controlled_buffer_1_out), .en(REGA_we), .Q(B), .clk(clk), .clr(RESET));
  Clock u_CLK (.out(clk));
  D_Flip_Flop d_ff_1 (.clk(clk), .D(and_2_out), .Q(Zero), .reset(RESET));  // open: Qn, preset, en
  and and_2 (and_2_out, ~alu_1_s[0], ~alu_1_s[1], ~alu_1_s[2], ~alu_1_s[3], ~alu_1_s[4], ~alu_1_s[5], ~alu_1_s[6], ~alu_1_s[7]);  // AND_Gate
endmodule

module Contador (
  input  Clock,
  input  Jump,
  input  [7:0] Jaddr,
  output [7:0] Address
);

  wire and_1_out, and_2_out, and_3_out, and_4_out, and_5_out, and_6_out, demultiplexer_1_out0,
       demultiplexer_1_out1, demultiplexer_2_out0, demultiplexer_2_out1, demultiplexer_3_out0,
       demultiplexer_3_out1, demultiplexer_4_out0, demultiplexer_4_out1, demultiplexer_5_out0,
       demultiplexer_5_out1, demultiplexer_6_out0, demultiplexer_6_out1, demultiplexer_7_out0,
       demultiplexer_7_out1, demultiplexer_8_out0, demultiplexer_8_out1;

  Demultiplexer #(.enable("false")) demultiplexer_1 (
    .out0(demultiplexer_1_out0), .out1(demultiplexer_1_out1), .in(Jump), .sel(Jaddr[0]));
  T_Flip_Flop t_ff_1 (
    .clk(Clock), .T(1'b1), .Q(Address[0]), .preset(demultiplexer_1_out1), .reset(demultiplexer_1_out0));  // open: Qn, en
  Demultiplexer #(.enable("false")) demultiplexer_2 (
    .out0(demultiplexer_2_out0), .out1(demultiplexer_2_out1), .in(Jump), .sel(Jaddr[1]));
  T_Flip_Flop t_ff_2 (
    .clk(Clock), .T(Address[0]), .Q(Address[1]), .preset(demultiplexer_2_out1), .reset(demultiplexer_2_out0));  // open: Qn, en
  and and_1 (and_1_out, Address[1], Address[0]);
  Demultiplexer #(.enable("false")) demultiplexer_3 (
    .out0(demultiplexer_3_out0), .out1(demultiplexer_3_out1), .in(Jump), .sel(Jaddr[2]));
  T_Flip_Flop t_ff_3 (
    .clk(Clock), .T(and_1_out), .Q(Address[2]), .preset(demultiplexer_3_out1), .reset(demultiplexer_3_out0));  // open: Qn, en
  and and_2 (and_2_out, Address[2], and_1_out);
  Demultiplexer #(.enable("false")) demultiplexer_4 (
    .out0(demultiplexer_4_out0), .out1(demultiplexer_4_out1), .in(Jump), .sel(Jaddr[3]));
  T_Flip_Flop t_ff_4 (
    .clk(Clock), .T(and_2_out), .Q(Address[3]), .preset(demultiplexer_4_out1), .reset(demultiplexer_4_out0));  // open: Qn, en
  and and_3 (and_3_out, Address[3], and_2_out);
  Demultiplexer #(.enable("false")) demultiplexer_5 (
    .out0(demultiplexer_5_out0), .out1(demultiplexer_5_out1), .in(Jump), .sel(Jaddr[4]));
  T_Flip_Flop t_ff_5 (
    .clk(Clock), .T(and_3_out), .Q(Address[4]), .preset(demultiplexer_5_out1), .reset(demultiplexer_5_out0));  // open: Qn, en
  and and_4 (and_4_out, Address[4], and_3_out);
  Demultiplexer #(.enable("false")) demultiplexer_6 (
    .out0(demultiplexer_6_out0), .out1(demultiplexer_6_out1), .in(Jump), .sel(Jaddr[5]));
  T_Flip_Flop t_ff_6 (
    .clk(Clock), .T(and_4_out), .Q(Address[5]), .preset(demultiplexer_6_out1), .reset(demultiplexer_6_out0));  // open: Qn, en
  and and_5 (and_5_out, Address[5], and_4_out);
  Demultiplexer #(.enable("false")) demultiplexer_7 (
    .out0(demultiplexer_7_out0), .out1(demultiplexer_7_out1), .in(Jump), .sel(Jaddr[6]));
  T_Flip_Flop t_ff_7 (
    .clk(Clock), .T(and_5_out), .Q(Address[6]), .preset(demultiplexer_7_out1), .reset(demultiplexer_7_out0));  // open: Qn, en
  and and_6 (and_6_out, Address[6], and_5_out);
  Demultiplexer #(.enable("false")) demultiplexer_8 (
    .out0(demultiplexer_8_out0), .out1(demultiplexer_8_out1), .in(Jump), .sel(Jaddr[7]));
  T_Flip_Flop t_ff_8 (
    .clk(Clock), .T(and_6_out), .Q(Address[7]), .preset(demultiplexer_8_out1), .reset(demultiplexer_8_out0));  // open: Qn, en

  // Other names for the same wires on the sheet: Q0 = Address[0]; Q1 = Address[1]; Q2 = Address[2]; Q3 = Address[3];
  //   Q4 = Address[4]; Q5 = Address[5]; Q6 = Address[6]; Q7 = Address[7]; J = Jump; Ja0 = Jaddr[0]; Ja1 = Jaddr[1];
  //   Ja2 = Jaddr[2]; Ja3 = Jaddr[3]; Ja4 = Jaddr[4]; Ja5 = Jaddr[5]; Ja6 = Jaddr[6]; Ja7 = Jaddr[7]
endmodule

module Banco_de_Registros (
  input  [7:0] IN,
  input  Clk,
  input  Rst,
  input  We,
  input  [3:0] Rd,
  input  [3:0] Rs,
  output [7:0] Out
);

  wire C0, C1, C2, C3, C4, C5, C6, C7, C8, C9, C10, C11, C12, C13, C14, C15, We0, We1, We2, We3, We4, We5,
       We6, We7, We8, We9, WeA, WeB, WeC, WeD, WeE, WeF;
  wire [7:0] Q0, Q1, Q2, Q3, Q4, Q5, Q6, Q7, Q8, Q9, QA, QB, QC, QD, QE, QF;

  Demultiplexer #(.select(4), .enable("false")) demultiplexer_1 (
    .out0(We0), .out1(We1), .out2(We2), .out3(We3), .out4(We4), .out5(We5), .out6(We6), .out7(We7),
    .out8(We8), .out9(We9), .out10(WeA), .out11(WeB), .out12(WeC), .out13(WeD), .out14(WeE), .out15(WeF),
    .in(We), .sel(Rd));
  Demultiplexer #(.select(4), .enable("false")) demultiplexer_2 (
    .out0(C0), .out1(C1), .out2(C2), .out3(C3), .out4(C4), .out5(C5), .out6(C6), .out7(C7), .out8(C8),
    .out9(C9), .out10(C10), .out11(C11), .out12(C12), .out13(C13), .out14(C14), .out15(C15), .in(1'b1),
    .sel(Rs));
  Register register_1 (.D(IN), .en(We0), .Q(Q0), .clk(Clk), .clr(Rst));
  Register register_2 (.D(IN), .en(We2), .Q(Q2), .clk(Clk), .clr(Rst));
  Register register_3 (.D(IN), .en(We4), .Q(Q4), .clk(Clk), .clr(Rst));
  Register register_4 (.D(IN), .en(We6), .Q(Q6), .clk(Clk), .clr(Rst));
  Register register_5 (.D(IN), .en(We8), .Q(Q8), .clk(Clk), .clr(Rst));
  Register register_6 (.D(IN), .en(WeA), .Q(QA), .clk(Clk), .clr(Rst));
  Register register_7 (.D(IN), .en(WeC), .Q(QC), .clk(Clk), .clr(Rst));
  Register register_8 (.D(IN), .en(WeE), .Q(QE), .clk(Clk), .clr(Rst));
  Register register_9 (.D(IN), .en(We1), .Q(Q1), .clk(Clk), .clr(Rst));
  Register register_10 (.D(IN), .en(We3), .Q(Q3), .clk(Clk), .clr(Rst));
  Register register_11 (.D(IN), .en(We5), .Q(Q5), .clk(Clk), .clr(Rst));
  Register register_12 (.D(IN), .en(We7), .Q(Q7), .clk(Clk), .clr(Rst));
  Register register_13 (.D(IN), .en(We9), .Q(Q9), .clk(Clk), .clr(Rst));
  Register register_14 (.D(IN), .en(WeB), .Q(QB), .clk(Clk), .clr(Rst));
  Register register_15 (.D(IN), .en(WeD), .Q(QD), .clk(Clk), .clr(Rst));
  Register register_16 (.D(IN), .en(WeF), .Q(QF), .clk(Clk), .clr(Rst));
  assign Out = C0 ? Q0 : 8'bz;  // Controlled_Buffer controlled_buffer_1
  assign Out = C1 ? Q1 : 8'bz;  // Controlled_Buffer controlled_buffer_2
  assign Out = C2 ? Q2 : 8'bz;  // Controlled_Buffer controlled_buffer_3
  assign Out = C3 ? Q3 : 8'bz;  // Controlled_Buffer controlled_buffer_4
  assign Out = C4 ? Q4 : 8'bz;  // Controlled_Buffer controlled_buffer_5
  assign Out = C5 ? Q5 : 8'bz;  // Controlled_Buffer controlled_buffer_6
  assign Out = C6 ? Q6 : 8'bz;  // Controlled_Buffer controlled_buffer_7
  assign Out = C7 ? Q7 : 8'bz;  // Controlled_Buffer controlled_buffer_8
  assign Out = C8 ? Q8 : 8'bz;  // Controlled_Buffer controlled_buffer_9
  assign Out = C9 ? Q9 : 8'bz;  // Controlled_Buffer controlled_buffer_10
  assign Out = C10 ? QA : 8'bz;  // Controlled_Buffer controlled_buffer_11
  assign Out = C11 ? QB : 8'bz;  // Controlled_Buffer controlled_buffer_12
  assign Out = C12 ? QC : 8'bz;  // Controlled_Buffer controlled_buffer_13
  assign Out = C13 ? QD : 8'bz;  // Controlled_Buffer controlled_buffer_14
  assign Out = C14 ? QE : 8'bz;  // Controlled_Buffer controlled_buffer_15
  assign Out = C15 ? QF : 8'bz;  // Controlled_Buffer controlled_buffer_16
endmodule

module ROM (
  input  clk,
  input  Jump,
  input  [7:0] J_Address,
  output [15:0] S
);

  wire [7:0] contador_1_address;

  Contador contador_1 (.Clock(clk), .Jump(Jump), .Jaddr(J_Address), .Address(contador_1_address));
  ROM_part #(.dataWidth(16)) rom_1 (.addr(contador_1_address), .data(S));  // open: sel

  // Notes on the sheet:
  //   contents of rom_1 (hex, n*v repeats v):
  //   130 500 1211 1222 508 1311 1322 501 1243 310e 2133 1122 3110 3008 1111 300a 210
endmodule

module _2_a_1_1bit (
  input  A,
  input  B,
  input  Ctrl,
  output S
);

  wire and_1_out, and_2_out;

  and and_1 (and_1_out, A, ~Ctrl);  // AND_Gate
  and and_2 (and_2_out, B, Ctrl);
  or or_1 (S, and_1_out, and_2_out);
endmodule

module ALU (
  input  [7:0] A,
  input  [7:0] B,
  input  Ctrl0,
  input  Ctrl1,
  input  Ctrl2,
  output [7:0] S,
  output Cout
);

  wire [7:0] A2_3, A4, A5, A6, n2_a_1_8bits_1_s, n2_a_1_8bits_2_s, n2_a_1_8bits_3_s, n2_a_1_8bits_4_s,
       n2_a_1_8bits_5_s, n2_a_1_8bits_6_s, xor_2_out;

  assign A6 = A ^ B;  // XOR_Gate xor_1, 8 bits wide
  _2_a_1_8bits u_2_a_1_8bits_1 (.A(A), .B({A[6:0], 1'b0}), .Ctrl(Ctrl0), .S(n2_a_1_8bits_1_s));
  _2_a_1_8bits u_2_a_1_8bits_2 (.A(A2_3), .B(A2_3), .Ctrl(Ctrl0), .S(n2_a_1_8bits_2_s));
  _2_a_1_8bits u_2_a_1_8bits_3 (.A(A4), .B(A5), .Ctrl(Ctrl0), .S(n2_a_1_8bits_3_s));
  _2_a_1_8bits u_2_a_1_8bits_4 (.A(A6), .B({1'b0, A[7:1]}), .Ctrl(Ctrl0), .S(n2_a_1_8bits_4_s));
  assign A5 = A | B;  // OR_Gate or_1, 8 bits wide
  _2_a_1_8bits u_2_a_1_8bits_5 (.A(n2_a_1_8bits_1_s), .B(n2_a_1_8bits_2_s), .Ctrl(Ctrl1), .S(n2_a_1_8bits_5_s));
  _2_a_1_8bits u_2_a_1_8bits_6 (.A(n2_a_1_8bits_3_s), .B(n2_a_1_8bits_4_s), .Ctrl(Ctrl1), .S(n2_a_1_8bits_6_s));
  assign xor_2_out = {8{Ctrl0}} ^ B;  // XOR_Gate xor_2, 8 bits wide
  _2_a_1_8bits u_2_a_1_8bits_7 (.A(n2_a_1_8bits_5_s), .B(n2_a_1_8bits_6_s), .Ctrl(Ctrl2), .S(S));
  Suma_8bits suma_8bits_1 (.Cout(Cout), .A(A), .B(xor_2_out), .Ctrl(Ctrl0), .R(A2_3));
  assign A4 = A & B;  // AND_Gate and_1, 8 bits wide

  // Other names for the same wires on the sheet: A1[7:1] = A[6:0]; A7[6:0] = A[7:1]
endmodule

module _2_a_1_8bits (
  input  [7:0] A,
  input  [7:0] B,
  input  Ctrl,
  output [7:0] S
);

  _2_a_1_1bit u_2_a_1_1bit_1 (.A(A[0]), .B(B[0]), .Ctrl(Ctrl), .S(S[0]));
  _2_a_1_1bit u_2_a_1_1bit_2 (.A(A[1]), .B(B[1]), .Ctrl(Ctrl), .S(S[1]));
  _2_a_1_1bit u_2_a_1_1bit_3 (.A(A[2]), .B(B[2]), .Ctrl(Ctrl), .S(S[2]));
  _2_a_1_1bit u_2_a_1_1bit_4 (.A(A[3]), .B(B[3]), .Ctrl(Ctrl), .S(S[3]));
  _2_a_1_1bit u_2_a_1_1bit_5 (.A(A[4]), .B(B[4]), .Ctrl(Ctrl), .S(S[4]));
  _2_a_1_1bit u_2_a_1_1bit_6 (.A(A[5]), .B(B[5]), .Ctrl(Ctrl), .S(S[5]));
  _2_a_1_1bit u_2_a_1_1bit_7 (.A(A[6]), .B(B[6]), .Ctrl(Ctrl), .S(S[6]));
  _2_a_1_1bit u_2_a_1_1bit_8 (.A(A[7]), .B(B[7]), .Ctrl(Ctrl), .S(S[7]));
endmodule

module Suma_1bit (
  input  A,
  input  B,
  input  Ce,
  output Ri,
  output Cs
);

  wire and_1_out, and_2_out, and_3_out, xor_1_out;

  xor xor_1 (xor_1_out, A, B);
  xor xor_2 (Ri, xor_1_out, Ce);
  and and_1 (and_1_out, A, B);
  and and_2 (and_2_out, B, Ce);
  and and_3 (and_3_out, A, Ce);
  or or_1 (Cs, and_1_out, and_2_out, and_3_out);
endmodule

module Suma_8bits (
  input  [7:0] A,
  input  [7:0] B,
  input  Ctrl,
  output [7:0] R,
  output Cout
);

  wire suma_1bit_1_cs, suma_1bit_2_cs, suma_1bit_3_cs, suma_1bit_4_cs, suma_1bit_5_cs, suma_1bit_6_cs,
       suma_1bit_7_cs;

  Suma_1bit suma_1bit_1 (.A(A[0]), .B(B[0]), .Ce(Ctrl), .Ri(R[0]), .Cs(suma_1bit_1_cs));
  Suma_1bit suma_1bit_2 (.A(A[1]), .B(B[1]), .Ce(suma_1bit_1_cs), .Ri(R[1]), .Cs(suma_1bit_2_cs));
  Suma_1bit suma_1bit_3 (.A(A[2]), .B(B[2]), .Ce(suma_1bit_2_cs), .Ri(R[2]), .Cs(suma_1bit_3_cs));
  Suma_1bit suma_1bit_4 (.A(A[3]), .B(B[3]), .Ce(suma_1bit_3_cs), .Ri(R[3]), .Cs(suma_1bit_4_cs));
  Suma_1bit suma_1bit_5 (.A(A[4]), .B(B[4]), .Ce(suma_1bit_4_cs), .Ri(R[4]), .Cs(suma_1bit_5_cs));
  Suma_1bit suma_1bit_6 (.A(A[5]), .B(B[5]), .Ce(suma_1bit_5_cs), .Ri(R[5]), .Cs(suma_1bit_6_cs));
  Suma_1bit suma_1bit_7 (.A(A[6]), .B(B[6]), .Ce(suma_1bit_6_cs), .Ri(R[6]), .Cs(suma_1bit_7_cs));
  Suma_1bit suma_1bit_8 (.A(A[7]), .B(B[7]), .Ce(suma_1bit_7_cs), .Ri(R[7]), .Cs(Cout));
endmodule
